# Fritzing sketch rgb-lamp (saved by Fritzing 0.9.3b)

parts:
  U2 = NodeMCU V1.0
  LED2 = LED - 5mm [color="Red (633nm)" package="5 mm [THT]"]

nets:
  N1: U2.D0, LED2.anode
  N2: U2.D1, U2.GND, U2.D7, LED2.cathode

custom parts:
  NodeMCU V1.0: ESP8266 based NodeMCU V1.0
